# Fritzing sketch Cancelas Saida VLN (saved by Fritzing 0.9.8b)

parts:
  M1 = RioRand LM2596
  M2 = RioRand LM2596
  M3 = RioRand LM2596
  M4 = RioRand LM2596
  F1 = FUSE [package=fuse_5mm]  # not connected
  Maluska1 = maluska dil miniaturrelais [part_number="DIL Mini RY" package=THT]
  Maluska2 = maluska dil miniaturrelais [part_number="DIL Mini RY" package=THT]
  KY-1 = Keyes Relay [part_number="Rele Saida 2" package=THT]
  KY-2 = Keyes Relay [package=THT]
  U1 = Sharp PC817 [package=THT]
  U2 = Sharp PC817 [package=THT]
  R1 = Resistor [tolerance=±5% resistance=100 package="0603 [SMD]"]
  R2 = Resistor [tolerance=±5% resistance=100 package="0603 [SMD]"]
  LED1 = LED - 5mm [color="Red (633nm)" current=0.030 package="5 mm [THT]"]
  LED2 = LED - 5mm [color="Red (633nm)" current=0.030 package="5 mm [THT]"]
  Raspberry_Pi_1 = Raspberry Pi 3 [part_number=RPI-3-V1.2]
  LED3 = smd LED [color="Blue (470nm)" package="1206 [SMD]"]
  R3 = Resistor [tolerance=±5% resistance=100 package="0603 [SMD]"]
  LED4 = smd LED [color="Green (560nm)" package="1206 [SMD]"]
  LED5 = smd LED [color="Green (560nm)" package="1206 [SMD]"]
  R4 = Resistor [tolerance=±5% resistance=100 package="0603 [SMD]"]
  R5 = Resistor [tolerance=±5% resistance=100 package="0603 [SMD]"]
  R6 = Resistor [tolerance=±5% resistance=1000 package="0603 [SMD]"]
  R7 = Resistor [tolerance=±5% resistance=1000 package="0603 [SMD]"]

nets:
  N1: M1.Pin_1, KY-1.C, KY-2.C
  N2: M1.Pin_2, M3.Pin_2
  N3: M1.Pin_4, M2.Pin_4, Maluska1.8, Maluska2.8
  N4: M4.Pin_3, KY-1.signal, KY-2.signal
  N5: Maluska1.1, Maluska2.1
  N6: Maluska1.4, R1.Pin_1
  N7: Maluska2.4, R2.Pin_1
  N8: KY-1.power, Raspberry_Pi_1.GPIO26
  N9: KY-2.power, Raspberry_Pi_1.GPIO19
  N10: U1.Pin_1, LED1.cathode
  N11: U1.Pin_2, R1.Pin_0
  N12: U1.Pin_4, Raspberry_Pi_1.GPIO20, R6.Pin_0
  N13: U1.Pin_3, U2.Pin_3
  N14: U2.Pin_1, LED2.cathode
  N15: U2.Pin_2, R2.Pin_0
  N16: U2.Pin_4, Raspberry_Pi_1.GPIO21, R7.Pin_0
  N17: LED1.anode, LED2.anode, Raspberry_Pi_1.5V
  N18: Raspberry_Pi_1.3v3, R6.Pin_1
  N19: Raspberry_Pi_1.GPIO5, R5.Pin_0
  N20: Raspberry_Pi_1.GPIO6, R4.Pin_0
  N21: Raspberry_Pi_1.GND, LED3.cathode, LED4.cathode, LED5.cathode
  N22: Raspberry_Pi_1.GPIO12, R3.Pin_0
  N23: LED4.anode, R5.Pin_1
  N24: LED5.anode, R4.Pin_1

notes:
  GPIO 0 do Reader - MIKE4 - 2
  GPIO 1do Reader - MIKE4 - 3
  G12V do Reader - MIKE4 - 1
  12V 4A Fonte HYAMA
  Saida 2 - Cabo sinal MIKE8 - 6
  Saida1 - Cabo sinal MIKE8 - 5
  Cabo 5V MIKE8 - 1e 2
  Cabo GND MIKE8 - 7 e 8
  Cabo sinal MIKE8 - 3
  Cabo sinal MIKE8 - 4
  Saida 2 - Sinal 12V para cancela Esquerda
  MIKE4 - 3+ e 4 GND
  Saida 1 - Sinal 12V para cancela Direita
  MIKE4 - 1+ e 2 GND

custom parts:
  Keyes Relay: The Keyes 5V relay module is suitable for SCM development, home appliance control. It uses a 5V~12V TIL control signal which can control DC / AC signal.
