# Fritzing sketch Sensor_Nivel_e_Vazao_Casa (saved by Fritzing 0.9.8b)

parts:
  U1 = NodeMCU V1.0
  YF-S201_Flow_Meter1 = YF-S201 Water Flow Meter
  HC-SR04_Sensor_1 = HC-SR04 Ultrasonic Distance Sensor
  U2 = LM2596 step down module

nets:
  3V3: U1.3V3, YF-S201_Flow_Meter1.VCC
  GND: U1.GND, YF-S201_Flow_Meter1.GND, U2.IN-, U2.OUT-
  N1: U1.D5, YF-S201_Flow_Meter1.SIG
  N2: U1.D7, HC-SR04_Sensor_1.TRIG
  N3: U1.D8, HC-SR04_Sensor_1.ECHO
  VIN: U1.Vin, HC-SR04_Sensor_1.VCC

custom parts:
  NodeMCU V1.0: ESP8266 based NodeMCU
  YF-S201 Water Flow Meter: The YF-S201 Flow Meter. The input voltage is 5V to 24V (DC).
  LM2596 step down module: LM2596 DC-DC step down power supply module 3 A.
