# Fritzing sketch Controle_Semaforos (saved by Fritzing 0.9.8b)

parts:
  Raspberry_Pi_2 = Raspberry Pi 3 [part_number=RPI-3-V1.2]
  M5 = RioRand LM2596
  M6 = RioRand LM2596
  M7 = RioRand LM2596
  M8 = RioRand LM2596
  F2 = FUSE [package=fuse_5mm]  # not connected
  Maluska3 = maluska dil miniaturrelais [part_number="DIL Mini RY" package=THT]
  Maluska4 = maluska dil miniaturrelais [part_number="DIL Mini RY" package=THT]
  KY-3 = Keyes Relay [package=THT]
  KY-4 = Keyes Relay [part_number="Rele Saida 2" package=THT]
  U3 = Sharp PC817 [package=THT]
  U4 = Sharp PC817 [package=THT]
  R8 = Resistor [tolerance=±5% resistance=100 package="0603 [SMD]"]
  R9 = Resistor [tolerance=±5% resistance=100 package="0603 [SMD]"]
  LED6 = LED - 5mm [color="Red (633nm)" current=0.030 package="5 mm [THT]"]
  LED7 = LED - 5mm [color="Red (633nm)" current=0.030 package="5 mm [THT]"]
  LED8 = smd LED [color="Blue (470nm)" package="1206 [SMD]"]
  R10 = Resistor [tolerance=±5% resistance=100 package="0603 [SMD]"]
  LED9 = smd LED [color="Green (560nm)" package="1206 [SMD]"]
  LED10 = smd LED [color="Green (560nm)" package="1206 [SMD]"]
  R11 = Resistor [tolerance=±5% resistance=100 package="0603 [SMD]"]
  R12 = Resistor [tolerance=±5% resistance=100 package="0603 [SMD]"]
  R13 = Resistor [tolerance=±5% resistance=1000 package="0603 [SMD]"]
  R14 = Resistor [tolerance=±5% resistance=1000 package="0603 [SMD]"]

nets:
  3V3: Raspberry_Pi_2.3v3, Raspberry_Pi_2.3V3, R13.Pin_1, R14.Pin_1
  N1: Raspberry_Pi_2.GPIO5, R11.Pin_0
  N2: Raspberry_Pi_2.GPIO6, R12.Pin_0
  N3: Raspberry_Pi_2.GPIO19, KY-3.power
  N4: Raspberry_Pi_2.GPIO26, KY-4.power
  N5: Raspberry_Pi_2.GPIO21, U4.Pin_4, R13.Pin_0
  N6: Raspberry_Pi_2.GPIO20, U3.Pin_4, R14.Pin_0
  N7: Raspberry_Pi_2.GND, LED8.cathode, LED9.cathode, LED10.cathode
  N8: Raspberry_Pi_2.GPIO12, R10.Pin_0
  N9: Raspberry_Pi_2.5V, LED6.anode, LED7.anode
  N10: M5.Pin_2, M8.Pin_2
  N11: M6.Pin_3, KY-3.signal, KY-4.signal
  N12: M7.Pin_3, M8.Pin_3
  N13: M7.Pin_4, M8.Pin_4, Maluska3.8, Maluska4.8
  N14: M8.Pin_1, KY-3.C, KY-4.C
  N15: Maluska3.1, Maluska4.1
  N16: Maluska3.4, R8.Pin_1
  N17: Maluska4.4, R9.Pin_1
  N18: U3.Pin_1, LED6.cathode
  N19: U3.Pin_2, R9.Pin_0
  N20: U3.Pin_3, U4.Pin_3
  N21: U4.Pin_1, LED7.cathode
  N22: U4.Pin_2, R8.Pin_0

notes:
  Saida 1 - Sinal 12V para cancela Direita
  MIKE4 - 1+ e 2 GND
  Saida 2 - Sinal 12V para cancela Esquerda
  MIKE4 - 3+ e 4 GND
  Cabo sinal MIKE8 - 4
  Cabo sinal MIKE8 - 3
  Cabo GND MIKE8 - 7 e 8
  Cabo 5V MIKE8 - 1e 2
  Saida1 - Cabo sinal MIKE8 - 5
  Saida 2 - Cabo sinal MIKE8 - 6
  12V 4A Fonte HYAMA
  G12V do Reader - MIKE4 - 1
  GPIO 1do Reader - MIKE4 - 3
  GPIO 0 do Reader - MIKE4 - 2

custom parts:
  Keyes Relay: The Keyes 5V relay module is suitable for SCM development, home appliance control. It uses a 5V~12V TIL control signal which can control DC / AC signal.
